# Fritzing sketch rgb-led-aht20-temp-hum-sensor-wiring (saved by Fritzing 0.9.3b)
breadboards: 1

parts:
  LED = RGB LED (com. cathode, rbg) [package="5 mm [THT]"]
  R2_blue = Resistor [tolerance=±5% resistance=330 package="0805 [SMD]"]
  R3_green = Resistor [tolerance=±5% resistance=330 package="0805 [SMD]"]
  Raspberry_Pi_4_model_B = Raspberry Pi 4 [part_number=RPI-4-b]
  Adafruit_T-Cobbler = Adafruit T-Cobbler Plus [part_number="Adafruit #1989 and #2028"]
  AHT20_sensor = DHT22 Humidity and Temperature Sensor
  R1_red = Resistor [tolerance=±5% resistance=330 package="0805 [SMD]"]

nets:
  N1: LED.red_anode, R3_green.Pin_0
  N2: LED.common_cathode, R2_blue.Pin_0
  GND: LED.blue_anode, Raspberry_Pi_4_model_B.GND, Adafruit_T-Cobbler.GPIO4, Adafruit_T-Cobbler.GND, AHT20_sensor.GND
  N3: LED.green_anode, R1_red.Pin_0
  N4: R2_blue.Pin_1, Raspberry_Pi_4_model_B.GPIO20, Adafruit_T-Cobbler.GPIO20
  N5: R3_green.Pin_1, Raspberry_Pi_4_model_B.GPIO16, Adafruit_T-Cobbler.GPIO16
  3V3: Raspberry_Pi_4_model_B.3v3, Adafruit_T-Cobbler.+3.3V, AHT20_sensor.VDD
  N6: Raspberry_Pi_4_model_B.GPIO2, Adafruit_T-Cobbler.SDA, AHT20_sensor.DATA
  N7: Raspberry_Pi_4_model_B.GPIO3, Adafruit_T-Cobbler.SCL, AHT20_sensor.NULL
  N8: Raspberry_Pi_4_model_B.GPIO21, Adafruit_T-Cobbler.GPIO21, R1_red.Pin_1

notes:
  RGB LED and AHT20 Sensor

custom parts:
  Raspberry Pi 4: The RPi4, a faster version of the awesome Raspberry Pi 2 B ARM Board with 40 pin gpio. Ready for special Raspberry Pi B+ and RPi2 Hat (Hardware attached (on) top)
  Adafruit T-Cobbler Plus: The Raspberry Pi has landed on the Maker World like a 40-GPIO pinned, quad-USB ported, credit card sized bomb of DIY joy. And while you can use most of our great Model B accessories by hooking up our downgrade cable, its probably a good time to upgrade your set up and accessorize using all of the 40 pins. That's why we now carry the Assembled Adafruit Pi T-Cobbler Plus - Breakout + Cable for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
